// Logisim project esp8266_clock.circ as structural Verilog: 5 circuits, main circuit main
module main (
);

  wire decoder_1_out0, decoder_1_out1, decoder_1_out2, decoder_1_out3, esp8266_nodemcu_v3_1_d1,
       esp8266_nodemcu_v3_1_d2, esp8266_nodemcu_v3_1_d3, esp8266_nodemcu_v3_1_d4, esp8266_nodemcu_v3_1_d5,
       esp8266_nodemcu_v3_1_d6, esp8266_nodemcu_v3_1_d7, ic74273_octal_d_ff_1_q0, ic74273_octal_d_ff_1_q1,
       ic74273_octal_d_ff_1_q2, ic74273_octal_d_ff_1_q3, ic74273_octal_d_ff_1_q4, ic74273_octal_d_ff_1_q5,
       ic74273_octal_d_ff_1_q6, ic74273_octal_d_ff_2_q0, ic74273_octal_d_ff_2_q1, ic74273_octal_d_ff_2_q2,
       ic74273_octal_d_ff_2_q3, ic74273_octal_d_ff_2_q4, ic74273_octal_d_ff_2_q5, ic74273_octal_d_ff_2_q6,
       ic74273_octal_d_ff_3_q0, ic74273_octal_d_ff_3_q1, ic74273_octal_d_ff_3_q2, ic74273_octal_d_ff_3_q3,
       ic74273_octal_d_ff_3_q4, ic74273_octal_d_ff_3_q5, ic74273_octal_d_ff_3_q6, ic74273_octal_d_ff_4_q0,
       ic74273_octal_d_ff_4_q1, ic74273_octal_d_ff_4_q2, ic74273_octal_d_ff_4_q3, ic74273_octal_d_ff_4_q4,
       ic74273_octal_d_ff_4_q5, ic74273_octal_d_ff_4_q6;
  wire [1:0] esp8266_nodemcu_v3_1_d0;

  IC74273_Octal_D_Flip_Flop ic74273_octal_d_ff_1 (
    .Clock(decoder_1_out3), .D0(esp8266_nodemcu_v3_1_d1), .Q0(ic74273_octal_d_ff_1_q0),
    .D1(esp8266_nodemcu_v3_1_d2), .Q1(ic74273_octal_d_ff_1_q1), .D2(esp8266_nodemcu_v3_1_d3),
    .Q2(ic74273_octal_d_ff_1_q2), .D3(esp8266_nodemcu_v3_1_d4), .Q3(ic74273_octal_d_ff_1_q3),
    .D4(esp8266_nodemcu_v3_1_d5), .Q4(ic74273_octal_d_ff_1_q4), .D5(esp8266_nodemcu_v3_1_d6),
    .Q5(ic74273_octal_d_ff_1_q5), .D6(esp8266_nodemcu_v3_1_d7), .Q6(ic74273_octal_d_ff_1_q6));  // open: Master_Reset, D7, Q7
  ESP8266_NodeMCU_V3 esp8266_nodemcu_v3_1 (
    .D0(esp8266_nodemcu_v3_1_d0[0]), .D1(esp8266_nodemcu_v3_1_d1), .D2(esp8266_nodemcu_v3_1_d2),
    .D3(esp8266_nodemcu_v3_1_d3), .D4(esp8266_nodemcu_v3_1_d4), .D5(esp8266_nodemcu_v3_1_d5),
    .D6(esp8266_nodemcu_v3_1_d6), .D7(esp8266_nodemcu_v3_1_d7), .D8(esp8266_nodemcu_v3_1_d0[1]));  // open: _3V, G, RX, TX, G_2, _3V_2, A0, G_3, VU, S3, S2, S1, CS, S0, SK, G_4, _3V_3, EN, RST, G_5, VIN
  IC74273_Octal_D_Flip_Flop ic74273_octal_d_ff_2 (
    .Clock(decoder_1_out2), .D0(esp8266_nodemcu_v3_1_d1), .Q0(ic74273_octal_d_ff_2_q0),
    .D1(esp8266_nodemcu_v3_1_d2), .Q1(ic74273_octal_d_ff_2_q1), .D2(esp8266_nodemcu_v3_1_d3),
    .Q2(ic74273_octal_d_ff_2_q2), .D3(esp8266_nodemcu_v3_1_d4), .Q3(ic74273_octal_d_ff_2_q3),
    .D4(esp8266_nodemcu_v3_1_d5), .Q4(ic74273_octal_d_ff_2_q4), .D5(esp8266_nodemcu_v3_1_d6),
    .Q5(ic74273_octal_d_ff_2_q5), .D6(esp8266_nodemcu_v3_1_d7), .Q6(ic74273_octal_d_ff_2_q6));  // open: Master_Reset, D7, Q7
  _7_Segment_Display u_7_segment_display_1 (
    .g(ic74273_octal_d_ff_1_q6), .f(ic74273_octal_d_ff_1_q5), .a(ic74273_octal_d_ff_1_q0),
    .b(ic74273_octal_d_ff_1_q1), .e(ic74273_octal_d_ff_1_q4), .d(ic74273_octal_d_ff_1_q3),
    .c(ic74273_octal_d_ff_1_q2));  // open: dp
  _7_Segment_Display u_7_segment_display_2 (
    .g(ic74273_octal_d_ff_2_q6), .f(ic74273_octal_d_ff_2_q5), .a(ic74273_octal_d_ff_2_q0),
    .b(ic74273_octal_d_ff_2_q1), .e(ic74273_octal_d_ff_2_q4), .d(ic74273_octal_d_ff_2_q3),
    .c(ic74273_octal_d_ff_2_q2));  // open: dp
  _7_Segment_Display u_7_segment_display_3 (
    .g(ic74273_octal_d_ff_3_q6), .f(ic74273_octal_d_ff_3_q5), .a(ic74273_octal_d_ff_3_q0),
    .b(ic74273_octal_d_ff_3_q1), .e(ic74273_octal_d_ff_3_q4), .d(ic74273_octal_d_ff_3_q3),
    .c(ic74273_octal_d_ff_3_q2));  // open: dp
  IC74273_Octal_D_Flip_Flop ic74273_octal_d_ff_3 (
    .Clock(decoder_1_out1), .D0(esp8266_nodemcu_v3_1_d1), .Q0(ic74273_octal_d_ff_3_q0),
    .D1(esp8266_nodemcu_v3_1_d2), .Q1(ic74273_octal_d_ff_3_q1), .D2(esp8266_nodemcu_v3_1_d3),
    .Q2(ic74273_octal_d_ff_3_q2), .D3(esp8266_nodemcu_v3_1_d4), .Q3(ic74273_octal_d_ff_3_q3),
    .D4(esp8266_nodemcu_v3_1_d5), .Q4(ic74273_octal_d_ff_3_q4), .D5(esp8266_nodemcu_v3_1_d6),
    .Q5(ic74273_octal_d_ff_3_q5), .D6(esp8266_nodemcu_v3_1_d7), .Q6(ic74273_octal_d_ff_3_q6));  // open: Master_Reset, D7, Q7
  _7_Segment_Display u_7_segment_display_4 (
    .g(ic74273_octal_d_ff_4_q6), .f(ic74273_octal_d_ff_4_q5), .a(ic74273_octal_d_ff_4_q0),
    .b(ic74273_octal_d_ff_4_q1), .e(ic74273_octal_d_ff_4_q4), .d(ic74273_octal_d_ff_4_q3),
    .c(ic74273_octal_d_ff_4_q2));  // open: dp
  Decoder #(.select(2)) decoder_1 (
    .out0(decoder_1_out0), .out1(decoder_1_out1), .out2(decoder_1_out2), .out3(decoder_1_out3),
    .sel(esp8266_nodemcu_v3_1_d0));  // open: en
  IC74273_Octal_D_Flip_Flop ic74273_octal_d_ff_4 (
    .Clock(decoder_1_out0), .D0(esp8266_nodemcu_v3_1_d1), .Q0(ic74273_octal_d_ff_4_q0),
    .D1(esp8266_nodemcu_v3_1_d2), .Q1(ic74273_octal_d_ff_4_q1), .D2(esp8266_nodemcu_v3_1_d3),
    .Q2(ic74273_octal_d_ff_4_q2), .D3(esp8266_nodemcu_v3_1_d4), .Q3(ic74273_octal_d_ff_4_q3),
    .D4(esp8266_nodemcu_v3_1_d5), .Q4(ic74273_octal_d_ff_4_q4), .D5(esp8266_nodemcu_v3_1_d6),
    .Q5(ic74273_octal_d_ff_4_q5), .D6(esp8266_nodemcu_v3_1_d7), .Q6(ic74273_octal_d_ff_4_q6));  // open: Master_Reset, D7, Q7
endmodule

module IC74273_Octal_D_Flip_Flop (
  input  D0,
  input  D1,
  input  D2,
  input  D3,
  input  Clock,
  input  Master_Reset,
  input  D4,
  input  D5,
  input  D6,
  input  D7,
  output Q0,
  output Q1,
  output Q2,
  output Q3,
  output Q4,
  output Q5,
  output Q6,
  output Q7
);

  D_Flip_Flop d_ff_1 (.clk(Clock), .D(D0), .Q(Q0), .reset(Master_Reset));  // open: Qn, preset, en
  D_Flip_Flop d_ff_2 (.clk(Clock), .D(D4), .Q(Q4), .reset(Master_Reset));  // open: Qn, preset, en
  D_Flip_Flop d_ff_3 (.clk(Clock), .D(D1), .Q(Q1), .reset(Master_Reset));  // open: Qn, preset, en
  D_Flip_Flop d_ff_4 (.clk(Clock), .D(D5), .Q(Q5), .reset(Master_Reset));  // open: Qn, preset, en
  D_Flip_Flop d_ff_5 (.clk(Clock), .D(D2), .Q(Q2), .reset(Master_Reset));  // open: Qn, preset, en
  D_Flip_Flop d_ff_6 (.clk(Clock), .D(D6), .Q(Q6), .reset(Master_Reset));  // open: Qn, preset, en
  D_Flip_Flop d_ff_7 (.clk(Clock), .D(D3), .Q(Q3), .reset(Master_Reset));  // open: Qn, preset, en
  D_Flip_Flop d_ff_8 (.clk(Clock), .D(D7), .Q(Q7), .reset(Master_Reset));  // open: Qn, preset, en
endmodule

module ESP8266_NodeMCU_V3 (
  output D0,
  output D1,
  output D2,
  output D3,
  output D4,
  output _3V,
  output G,
  output D5,
  output D6,
  output D7,
  output D8,
  output RX,
  output TX,
  output G_2,
  output _3V_2,
  output A0,
  output G_3,
  output VU,
  output S3,
  output S2,
  output S1,
  output CS,
  output S0,
  output SK,
  output G_4,
  output _3V_3,
  output EN,
  output RST,
  output G_5,
  output VIN
);

  wire clock_1_out, clock_2_a1, clock_2_a2, clock_2_a3, clock_2_a4, clock_2_b1, clock_2_b2, clock_2_b3,
       clock_2_b4, clock_2_c1, clock_2_c2, clock_2_c3, clock_2_c4, clock_2_d1, clock_2_d2, clock_2_d3,
       clock_2_d4, multiplexer_1_out, multiplexer_2_out, multiplexer_3_out, multiplexer_4_out;
  wire [1:0] adder_1_out, bit_extender_1_out;

  Clock_part clock_1 (.out(clock_1_out));
  Register #(.width(2)) register_1 (.D(adder_1_out), .Q({D8, D0}), .clk(clock_1_out));  // open: en, clr
  assign bit_extender_1_out = {{1{1'b0}}, 1'b1};  // Bit_Extender bit_extender_1
  Clock clock_2 (
    .D4(clock_2_d4), .D3(clock_2_d3), .D2(clock_2_d2), .D1(clock_2_d1), .C4(clock_2_c4), .C3(clock_2_c3),
    .C2(clock_2_c2), .C1(clock_2_c1), .B4(clock_2_b4), .B3(clock_2_b3), .B2(clock_2_b2), .B1(clock_2_b1),
    .A4(clock_2_a4), .A3(clock_2_a3), .A2(clock_2_a2), .A1(clock_2_a1));
  Adder #(.width(2)) adder_1 (.a({D8, D0}), .b(bit_extender_1_out), .out(adder_1_out));  // open: cin, cout
  Multiplexer #(.select(2)) multiplexer_1 (
    .in0(clock_2_a4), .in1(clock_2_b4), .in2(clock_2_c4), .in3(clock_2_d4), .out(multiplexer_1_out),
    .sel({D8, D0}));  // open: en
  Multiplexer #(.select(2)) multiplexer_2 (
    .in0(clock_2_a3), .in1(clock_2_b3), .in2(clock_2_c3), .in3(clock_2_d3), .out(multiplexer_2_out),
    .sel({D8, D0}));  // open: en
  Multiplexer #(.select(2)) multiplexer_3 (
    .in0(clock_2_a2), .in1(clock_2_b2), .in2(clock_2_c2), .in3(clock_2_d2), .out(multiplexer_3_out),
    .sel({D8, D0}));  // open: en
  Multiplexer #(.select(2)) multiplexer_4 (
    .in0(clock_2_a1), .in1(clock_2_b1), .in2(clock_2_c1), .in3(clock_2_d1), .out(multiplexer_4_out),
    .sel({D8, D0}));  // open: en
  BCD_to_7_segment_Converter bcd_to_7_segment_converter_1 (
    .D(multiplexer_1_out), .C(multiplexer_2_out), .B(multiplexer_3_out), .A(multiplexer_4_out), .a_2(D1),
    .b_2(D2), .c_2(D3), .d_2(D4), .e(D5), .f(D6), .g(D7));

  assign _3V = 1'b1;
  assign _3V_2 = 1'b1;
  assign _3V_3 = 1'b1;
  assign G = 1'b0;
  assign G_2 = 1'b0;
  assign G_4 = 1'b0;
  assign G_5 = 1'b0;
endmodule

module Clock (
  output D4,
  output D3,
  output D2,
  output D1,
  output C4,
  output C3,
  output C2,
  output C1,
  output B4,
  output B3,
  output B2,
  output B1,
  output A4,
  output A3,
  output A2,
  output A1
);

  wire and_1_out, and_2_out, and_3_out, and_4_out, and_5_out, clock_1_out, d_ff_1_qn, d_ff_2_q, d_ff_2_qn,
       d_ff_3_qn, d_ff_4_q, d_ff_4_qn, d_ff_5_qn, d_ff_6_q, d_ff_6_qn, d_ff_7_qn, d_ff_8_qn, d_ff_9_q,
       d_ff_9_qn, d_ff_10_q, d_ff_10_qn, d_ff_11_qn, d_ff_12_q, d_ff_12_qn, d_ff_13_qn, d_ff_14_qn,
       d_ff_15_qn, d_ff_16_qn, d_ff_17_qn, d_ff_18_qn, not_1_out, not_2_out, not_3_out, not_4_out, not_5_out,
       not_6_out, not_7_out, or_1_out;

  and and_1 (and_1_out, B3, A3, A4);
  D_Flip_Flop d_ff_1 (.clk(and_2_out), .D(d_ff_1_qn), .Q(A4), .Qn(d_ff_1_qn), .reset(and_1_out));  // open: preset, en
  Clock_part clock_1 (.out(clock_1_out));
  D_Flip_Flop d_ff_2 (
    .clk(clock_1_out), .D(d_ff_2_qn), .Q(d_ff_2_q), .Qn(d_ff_2_qn), .reset(and_4_out));  // open: preset, en
  not not_1 (not_1_out, C3);
  and and_2 (and_2_out, D3, not_1_out, B3, not_2_out);
  not not_2 (not_2_out, A3);
  D_Flip_Flop d_ff_3 (
    .clk(and_3_out), .D(d_ff_3_qn), .Q(A3), .Qn(d_ff_3_qn), .preset(and_1_out), .reset(and_2_out));  // open: en
  D_Flip_Flop d_ff_4 (
    .clk(d_ff_2_qn), .D(d_ff_4_qn), .Q(d_ff_4_q), .Qn(d_ff_4_qn), .reset(and_4_out));  // open: preset, en
  D_Flip_Flop d_ff_5 (.clk(d_ff_3_qn), .D(d_ff_5_qn), .Q(B3), .Qn(d_ff_5_qn), .reset(or_1_out));  // open: preset, en
  or or_1 (or_1_out, and_2_out, and_1_out);
  D_Flip_Flop d_ff_6 (
    .clk(d_ff_4_qn), .D(d_ff_6_qn), .Q(d_ff_6_q), .Qn(d_ff_6_qn), .reset(and_4_out));  // open: preset, en
  D_Flip_Flop d_ff_7 (.clk(d_ff_5_qn), .D(d_ff_7_qn), .Q(C3), .Qn(d_ff_7_qn), .reset(or_1_out));  // open: preset, en
  D_Flip_Flop d_ff_8 (.clk(d_ff_7_qn), .D(d_ff_8_qn), .Q(D3), .Qn(d_ff_8_qn), .reset(or_1_out));  // open: preset, en
  D_Flip_Flop d_ff_9 (
    .clk(d_ff_6_qn), .D(d_ff_9_qn), .Q(d_ff_9_q), .Qn(d_ff_9_qn), .reset(and_4_out));  // open: preset, en
  and and_3 (and_3_out, C2, B2, not_3_out);
  not not_3 (not_3_out, A2);
  D_Flip_Flop d_ff_10 (
    .clk(d_ff_9_qn), .D(d_ff_10_qn), .Q(d_ff_10_q), .Qn(d_ff_10_qn), .reset(and_4_out));  // open: preset, en
  D_Flip_Flop d_ff_11 (
    .clk(and_5_out), .D(d_ff_11_qn), .Q(A2), .Qn(d_ff_11_qn), .reset(and_3_out));  // open: preset, en
  D_Flip_Flop d_ff_12 (
    .clk(d_ff_10_qn), .D(d_ff_12_qn), .Q(d_ff_12_q), .Qn(d_ff_12_qn), .reset(and_4_out));  // open: preset, en
  D_Flip_Flop d_ff_13 (
    .clk(d_ff_11_qn), .D(d_ff_13_qn), .Q(B2), .Qn(d_ff_13_qn), .reset(and_3_out));  // open: preset, en
  D_Flip_Flop d_ff_14 (
    .clk(d_ff_13_qn), .D(d_ff_14_qn), .Q(C2), .Qn(d_ff_14_qn), .reset(and_3_out));  // open: preset, en
  not not_4 (not_4_out, d_ff_2_q);
  not not_5 (not_5_out, d_ff_4_q);
  and and_4 (and_4_out, not_4_out, not_5_out, d_ff_6_q, d_ff_9_q, d_ff_10_q, d_ff_12_q);
  and and_5 (and_5_out, D1, not_6_out, B1, not_7_out);
  not not_6 (not_6_out, C1);
  not not_7 (not_7_out, A1);
  D_Flip_Flop d_ff_15 (
    .clk(and_4_out), .D(d_ff_15_qn), .Q(A1), .Qn(d_ff_15_qn), .reset(and_5_out));  // open: preset, en
  D_Flip_Flop d_ff_16 (
    .clk(d_ff_15_qn), .D(d_ff_16_qn), .Q(B1), .Qn(d_ff_16_qn), .reset(and_5_out));  // open: preset, en
  D_Flip_Flop d_ff_17 (
    .clk(d_ff_16_qn), .D(d_ff_17_qn), .Q(C1), .Qn(d_ff_17_qn), .reset(and_5_out));  // open: preset, en
  D_Flip_Flop d_ff_18 (
    .clk(d_ff_17_qn), .D(d_ff_18_qn), .Q(D1), .Qn(d_ff_18_qn), .reset(and_5_out));  // open: preset, en

  assign B4 = 1'b0;
  assign C4 = 1'b0;
  assign D2 = 1'b0;
  assign D4 = 1'b0;
endmodule

module BCD_to_7_segment_Converter (
  input  D,
  input  C,
  input  B,
  input  A,
  output a_2,
  output b_2,
  output c_2,
  output d_2,
  output e,
  output f,
  output g
);

  wire nand_1_out, nand_2_out, nand_3_out, nand_4_out, nand_5_out, nand_6_out, nand_7_out, nand_8_out,
       nand_9_out, nand_10_out, nand_11_out, nand_12_out, nand_13_out, nand_14_out, nand_15_out, nand_16_out,
       nand_17_out, nand_18_out, nand_19_out, nand_20_out, nand_21_out, nand_22_out, nand_23_out,
       nand_24_out, nand_25_out, nand_26_out, nand_27_out, nand_28_out, nand_29_out, nand_30_out,
       nand_31_out, nand_32_out, nand_33_out, nand_34_out, nand_35_out, nand_36_out, nand_37_out,
       nand_38_out, nand_39_out, nand_40_out, nand_41_out, nand_42_out, nand_43_out, nand_44_out,
       nand_45_out, nand_46_out, nand_47_out, nand_48_out, nand_49_out, nand_50_out, nand_51_out,
       nand_52_out, nand_53_out, nand_54_out, nand_55_out, nand_56_out, nand_57_out, nand_58_out,
       nand_59_out, nand_60_out, nand_61_out, nand_62_out, nand_63_out, nand_64_out, nand_65_out,
       nand_66_out, nand_67_out, nand_68_out, nand_69_out, nand_70_out, nand_71_out, nand_72_out,
       nand_73_out, nand_74_out, nand_75_out, nand_76_out, nand_77_out, nand_78_out, nand_79_out,
       nand_80_out, nand_81_out, nand_82_out, nand_83_out, nand_84_out, nand_85_out, nand_86_out,
       nand_87_out, nand_88_out, nand_89_out, nand_90_out, nand_91_out, nand_92_out, nand_93_out,
       nand_94_out, nand_95_out, nand_96_out, nand_97_out, nand_98_out, nand_99_out, nand_100_out,
       nand_101_out, nand_102_out, nand_103_out, nand_104_out, nand_106_out, nand_107_out, nand_108_out,
       nand_109_out, nand_110_out, nand_111_out, nand_112_out, nand_113_out, nand_114_out, nand_115_out,
       nand_116_out, nand_117_out, nand_118_out, nand_119_out, nand_120_out, nand_121_out, nand_122_out,
       nand_123_out, nand_124_out, nand_125_out, nand_126_out, nand_127_out, nand_128_out, nand_129_out,
       nand_130_out, nand_131_out, nand_132_out, nand_133_out, nand_134_out, nand_136_out, nand_137_out,
       nand_138_out, nand_139_out, nand_141_out, nand_142_out, nand_143_out, nand_144_out, nand_145_out,
       nand_146_out, nand_147_out, nand_148_out;

  nand nand_1 (nand_1_out, C, C);
  nand nand_2 (nand_2_out, D, D);
  nand nand_3 (nand_3_out, B, B);
  nand nand_4 (nand_4_out, D, D);
  nand nand_5 (nand_5_out, B, B);
  nand nand_6 (nand_6_out, D, D);
  nand nand_7 (nand_7_out, D, D);
  nand nand_8 (nand_8_out, C, C);
  nand nand_9 (nand_9_out, C, C);
  nand nand_10 (nand_10_out, C, C);
  nand nand_11 (nand_11_out, A, A);
  nand nand_12 (nand_12_out, A, A);
  nand nand_13 (nand_13_out, D, D);
  nand nand_14 (nand_14_out, C, C);
  nand nand_15 (nand_15_out, A, A);
  nand nand_16 (nand_16_out, D, D);
  nand nand_17 (nand_17_out, D, nand_1_out);
  nand nand_18 (nand_18_out, nand_2_out, nand_3_out);
  nand nand_19 (nand_19_out, nand_4_out, nand_5_out);
  nand nand_20 (nand_20_out, nand_6_out, A);
  nand nand_21 (nand_21_out, nand_7_out, nand_8_out);
  nand nand_22 (nand_22_out, nand_9_out, B);
  nand nand_23 (nand_23_out, nand_10_out, nand_11_out);
  nand nand_24 (nand_24_out, B, nand_12_out);
  nand nand_25 (nand_25_out, D, B);
  nand nand_26 (nand_26_out, D, C);
  nand nand_27 (nand_27_out, nand_13_out, C);
  nand nand_28 (nand_28_out, nand_14_out, B);
  nand nand_29 (nand_29_out, B, nand_15_out);
  nand nand_30 (nand_30_out, nand_16_out, C);
  nand nand_31 (nand_31_out, C, C);
  nand nand_32 (nand_32_out, A, A);
  nand nand_33 (nand_33_out, D, D);
  nand nand_34 (nand_34_out, D, D);
  nand nand_35 (nand_35_out, nand_17_out, nand_17_out);
  nand nand_36 (nand_36_out, B, B);
  nand nand_37 (nand_37_out, D, D);
  nand nand_38 (nand_38_out, C, C);
  nand nand_39 (nand_39_out, nand_18_out, nand_18_out);
  nand nand_40 (nand_40_out, A, A);
  nand nand_41 (nand_41_out, D, D);
  nand nand_42 (nand_42_out, B, B);
  nand nand_43 (nand_43_out, nand_19_out, nand_20_out);
  nand nand_44 (nand_44_out, B, B);
  nand nand_45 (nand_45_out, D, D);
  nand nand_46 (nand_46_out, C, C);
  nand nand_47 (nand_47_out, nand_21_out, nand_21_out);
  nand nand_48 (nand_48_out, A, A);
  nand nand_49 (nand_49_out, nand_22_out, nand_22_out);
  nand nand_50 (nand_50_out, B, B);
  nand nand_51 (nand_51_out, B, B);
  nand nand_52 (nand_52_out, nand_23_out, nand_24_out);
  nand nand_53 (nand_53_out, nand_25_out, nand_26_out);
  nand nand_54 (nand_54_out, B, B);
  nand nand_55 (nand_55_out, A, A);
  nand nand_56 (nand_56_out, nand_27_out, nand_27_out);
  nand nand_57 (nand_57_out, B, B);
  nand nand_58 (nand_58_out, nand_28_out, nand_29_out);
  nand nand_59 (nand_59_out, nand_30_out, nand_30_out);
  nand nand_60 (nand_60_out, B, B);
  nand nand_61 (nand_61_out, C, C);
  nand nand_62 (nand_62_out, nand_31_out, nand_32_out);
  nand nand_63 (nand_63_out, nand_33_out, B);
  nand nand_64 (nand_64_out, nand_34_out, C);
  nand nand_65 (nand_65_out, C, B);
  nand nand_66 (nand_66_out, nand_35_out, nand_36_out);
  nand nand_67 (nand_67_out, nand_37_out, nand_38_out);
  nand nand_68 (nand_68_out, nand_39_out, nand_40_out);
  nand nand_69 (nand_69_out, nand_41_out, B);
  nand nand_70 (nand_70_out, D, nand_42_out);
  nand nand_71 (nand_71_out, nand_43_out, nand_43_out);
  nand nand_72 (nand_72_out, nand_44_out, A);
  nand nand_73 (nand_73_out, nand_45_out, C);
  nand nand_74 (nand_74_out, D, nand_46_out);
  nand nand_75 (nand_75_out, nand_47_out, nand_48_out);
  nand nand_76 (nand_76_out, nand_49_out, A);
  nand nand_77 (nand_77_out, C, nand_50_out);
  nand nand_78 (nand_78_out, C, B);
  nand nand_79 (nand_79_out, D, nand_51_out);
  nand nand_80 (nand_80_out, nand_52_out, nand_52_out);
  nand nand_81 (nand_81_out, nand_53_out, nand_53_out);
  nand nand_82 (nand_82_out, nand_54_out, nand_55_out);
  nand nand_83 (nand_83_out, nand_56_out, nand_57_out);
  nand nand_84 (nand_84_out, nand_58_out, nand_58_out);
  nand nand_85 (nand_85_out, nand_59_out, nand_60_out);
  nand nand_86 (nand_86_out, D, nand_61_out);
  nand nand_87 (nand_87_out, D, A);
  nand nand_88 (nand_88_out, nand_62_out, nand_63_out);
  nand nand_89 (nand_89_out, nand_64_out, nand_64_out);
  nand nand_90 (nand_90_out, nand_65_out, nand_66_out);
  nand nand_91 (nand_91_out, A, A);
  nand nand_92 (nand_92_out, nand_67_out, nand_68_out);
  nand nand_93 (nand_93_out, C, C);
  nand nand_94 (nand_94_out, A, A);
  nand nand_95 (nand_95_out, nand_69_out, nand_69_out);
  nand nand_96 (nand_96_out, nand_70_out, nand_70_out);
  nand nand_97 (nand_97_out, nand_71_out, nand_72_out);
  nand nand_98 (nand_98_out, nand_73_out, nand_74_out);
  nand nand_99 (nand_99_out, nand_75_out, nand_76_out);
  nand nand_100 (nand_100_out, nand_77_out, nand_77_out);
  nand nand_101 (nand_101_out, nand_78_out, nand_78_out);
  nand nand_102 (nand_102_out, A, A);
  nand nand_103 (nand_103_out, nand_79_out, nand_79_out);
  nand nand_104 (nand_104_out, A, A);
  nand nand_105 (e, nand_80_out, nand_81_out);
  nand nand_106 (nand_106_out, nand_82_out, nand_83_out);
  nand nand_107 (nand_107_out, A, A);
  nand nand_108 (nand_108_out, C, C);
  nand nand_109 (nand_109_out, nand_84_out, nand_85_out);
  nand nand_110 (nand_110_out, nand_86_out, nand_87_out);
  nand nand_111 (nand_111_out, nand_88_out, nand_88_out);
  nand nand_112 (nand_112_out, nand_89_out, A);
  nand nand_113 (nand_113_out, nand_90_out, nand_90_out);
  nand nand_114 (nand_114_out, D, nand_91_out);
  nand nand_115 (nand_115_out, nand_92_out, nand_92_out);
  nand nand_116 (nand_116_out, nand_93_out, nand_94_out);
  nand nand_117 (nand_117_out, nand_95_out, A);
  nand nand_118 (nand_118_out, nand_96_out, A);
  nand nand_119 (nand_119_out, nand_97_out, nand_97_out);
  nand nand_120 (nand_120_out, nand_98_out, nand_98_out);
  nand nand_121 (nand_121_out, nand_99_out, nand_99_out);
  nand nand_122 (nand_122_out, nand_100_out, A);
  nand nand_123 (nand_123_out, nand_101_out, nand_102_out);
  nand nand_124 (nand_124_out, nand_103_out, nand_104_out);
  nand nand_125 (nand_125_out, nand_106_out, nand_106_out);
  nand nand_126 (nand_126_out, C, nand_107_out);
  nand nand_127 (nand_127_out, D, nand_108_out);
  nand nand_128 (nand_128_out, D, B);
  nand nand_129 (nand_129_out, nand_109_out, nand_109_out);
  nand nand_130 (nand_130_out, nand_110_out, nand_110_out);
  nand nand_131 (nand_131_out, nand_111_out, nand_112_out);
  nand nand_132 (nand_132_out, nand_113_out, nand_114_out);
  nand nand_133 (nand_133_out, nand_115_out, nand_116_out);
  nand nand_134 (nand_134_out, nand_117_out, nand_118_out);
  nand nand_135 (c_2, nand_119_out, nand_120_out);
  nand nand_136 (nand_136_out, nand_121_out, nand_122_out);
  nand nand_137 (nand_137_out, nand_123_out, nand_124_out);
  nand nand_138 (nand_138_out, nand_125_out, nand_126_out);
  nand nand_139 (nand_139_out, nand_127_out, nand_128_out);
  nand nand_140 (g, nand_129_out, nand_130_out);
  nand nand_141 (nand_141_out, nand_131_out, nand_131_out);
  nand nand_142 (nand_142_out, nand_132_out, nand_132_out);
  nand nand_143 (nand_143_out, nand_133_out, nand_133_out);
  nand nand_144 (nand_144_out, nand_134_out, nand_134_out);
  nand nand_145 (nand_145_out, nand_136_out, nand_136_out);
  nand nand_146 (nand_146_out, nand_137_out, nand_137_out);
  nand nand_147 (nand_147_out, nand_138_out, nand_138_out);
  nand nand_148 (nand_148_out, nand_139_out, nand_139_out);
  nand nand_149 (a_2, nand_141_out, nand_142_out);
  nand nand_150 (b_2, nand_143_out, nand_144_out);
  nand nand_151 (d_2, nand_145_out, nand_146_out);
  nand nand_152 (f, nand_147_out, nand_148_out);

  // Notes on the sheet:
  //   Visit: http://github.com/marceloboeira for more examples
endmodule
